# Fritzing sketch arduino-parking (saved by Fritzing 0.9.1b)
breadboards: 1

parts:
  Part1 = Arduino Uno (Rev3)
  Part3 = SRF05 Ultrasonic Rangefinder
  LED1 = smd LED [color="Red (633nm)" package="1206 [SMD]"]
  LED2 = smd LED [color="Red (633nm)" package="1206 [SMD]"]
  LED3 = smd LED [color="Yellow (595nm)" package="1206 [SMD]"]
  LED4 = smd LED [color="Yellow (595nm)" package="1206 [SMD]"]
  LED5 = smd LED [color="Green (570nm)" package="1206 [SMD]"]
  LED6 = smd LED [color="Green (570nm)" package="1206 [SMD]"]
  R1 = Resistor [package="2010 [SMD]"]
  R2 = Resistor [package="2010 [SMD]"]
  R3 = Resistor [package="2010 [SMD]"]
  R4 = Resistor [package="2010 [SMD]"]
  R5 = Resistor [package="2010 [SMD]"]
  R6 = Resistor [package="2010 [SMD]"]
  J1 = Piezo Speaker

nets:
  N1: Part1.D8, R2.Pin_0
  N2: Part1.D9_PWM, R3.Pin_0
  N3: Part1.D10_PWM/SS, R4.Pin_0
  N4: Part1.D11_PWM/MOSI, R6.Pin_0
  N5: Part1.D12/MISO, R1.Pin_0
  N6: Part1.D13/SCK, R5.Pin_0
  N7: Part1.D3_PWM, Part3.Echo
  N8: Part1.D4, Part3.Trig
  N9: Part1.D6_PWM, J1.pin2
  5V: Part1.5V, Part3.VCC
  GND: Part1.GND, Part3.GND, LED1.cathode, LED2.cathode, LED3.cathode, LED5.cathode, LED6.cathode, J1.pin1
  N10: LED1.anode, R2.Pin_1
  N11: LED2.anode, R3.Pin_1
  N12: LED3.anode, R4.Pin_1
  N13: LED4.anode, R6.Pin_1
  N14: LED5.anode, R1.Pin_1
  N15: LED6.anode, R5.Pin_1
