# Fritzing sketch rapsb (saved by Fritzing 0.9.1b)
breadboards: 1

parts:
  Raspberry_Pi_B_rev1 = Raspberry Pi B rev1
  LED2 = smd LED [color="Green (570nm)" package="0805 [SMD]"]
  LED1 = smd LED [color="Red (633nm)" package="1206 [SMD]"]
  R1 = Resistor [package="0402 [SMD]"]
  R2 = Resistor [package="0402 [SMD]"]

nets:
  N1: Raspberry_Pi_B_rev1.GND, LED2.anode, LED1.anode
  N2: Raspberry_Pi_B_rev1.GPIO_17, R2.Pin_0
  N3: Raspberry_Pi_B_rev1.GPIO_18, R1.Pin_0
  N4: LED2.cathode, R1.Pin_1
  N5: LED1.cathode, R2.Pin_1
